# Fritzing sketch temperatur_humidity_PCB (saved by Fritzing 0.9.3b)
breadboards: 2

parts:
  Part1 = Arduino Uno (Rev3) - ICSP
  DHT1 = DHT11 Humitidy and Temperature Sensor
  LCD1 = LCD screen
  LED1 = smd LED [color="Red (633nm)" package="1206 [SMD]"]
  LED2 = smd LED [color="Yellow (585nm)" package="1206 [SMD]"]
  LED3 = smd LED [color="Green (555nm)" package="1206 [SMD]"]

nets:
  N1: Part1.A0, DHT1.DATA
  N2: Part1.ICSP_MISO, Part1.D12/MISO, LCD1.RS
  N3: Part1.D8, LED2.cathode
  N4: Part1.D9_PWM, LED1.cathode
  N5: Part1.D11_PWM/MOSI, LCD1.E
  GND: Part1.GND, DHT1.GND, LCD1.VSS, LCD1.V0, LCD1.R/W, LCD1.LED-, LED1.anode, LED2.anode, LED3.anode
  N6: Part1.D2, LCD1.DB7
  N7: Part1.D3_PWM, LCD1.DB6
  N8: Part1.D4, LCD1.DB5
  N9: Part1.D5_PWM, LCD1.DB4
  N10: Part1.D7, LED3.cathode
  VDD: Part1.5V, DHT1.VDD, LCD1.VDD, LCD1.LED+

custom parts:
  DHT11 Humitidy and Temperature Sensor: DHT11 Humidity and Temperature Sensor

// code stored in the sketch: FU6X0TMIOLRB0HR.ino
#include <LiquidCrystal.h>
#include <DHT.h>

#include "DHT.h"

#define DHTPIN A0     // what pin we're connected to

#define DHTTYPE DHT11   // DHT 11


LiquidCrystal lcd(12, 11, 5, 4, 3, 2);

DHT dht(DHTPIN, DHTTYPE);

void setup()
{
  Serial.begin(9600);
  for (int DigitalPin = 7; DigitalPin <= 9; DigitalPin++) 
 {
  pinMode(DigitalPin, OUTPUT);
 }
  lcd.begin(16,2); //16 by 2 character display
  
dht.begin();
}
 
void loop()
{
  delay(1000);
  // Reading temperature or humidity takes about 250 milliseconds!
  // Sensor readings may also be up to 2 seconds 'old' (its a very slow sensor)
  float h = dht.readHumidity();
  // Read temperature as Celsius (the default)
  float t = dht.readTemperature();

  lcd.clear();
  lcd.setCursor(0,0);
  lcd.print("Temp: ");
  lcd.print(t);
  lcd.print("'C");
  
  lcd.setCursor(0,1);
  lcd.print("Humid: ");
  lcd.print(h);
  lcd.print("%");
  
  if (t<=22)
  {
  digitalWrite(7, HIGH);
  digitalWrite(8, LOW);
  digitalWrite(9, LOW);
  }
  else if (t>22)
  {
  digitalWrite(8, HIGH);
  digitalWrite(7, LOW);
  digitalWrite(9, LOW);
  }
  else if (t>=35)
  {
  digitalWrite(9, HIGH);
  digitalWrite(7, LOW);
  digitalWrite(8, LOW);
  } 
  
}

// code stored in the sketch: TemperaturandHumidityCODE.ino
#include <LiquidCrystal.h>
#include <DHT.h>

#include "DHT.h"

#define DHTPIN A0     

#define DHTTYPE DHT11   // DHT 11


LiquidCrystal lcd(12, 11, 5, 4, 3, 2);

DHT dht(DHTPIN, DHTTYPE);

void setup()
{
  Serial.begin(9600);
  for (int DigitalPin = 7; DigitalPin <= 9; DigitalPin++) 
 {
  pinMode(DigitalPin, OUTPUT);
 }
  lcd.begin(16,2); //16 by 2 LCD
  
dht.begin();
}
 
void loop()
{
  delay(1000);
  
  
  float h = dht.readHumidity();
  // Read temperature as Celsius (default)
  float t = dht.readTemperature();

  lcd.clear();
  lcd.setCursor(0,0);
  lcd.print("Temp: ");
  lcd.print(t);
  lcd.print("'C");
  
  lcd.setCursor(0,1);
  lcd.print("Humid: ");
  lcd.print(h);
  lcd.print("%");
  
  if (t<=22)
  {
  digitalWrite(7, HIGH);
  digitalWrite(8, LOW);
  digitalWrite(9, LOW);
  }
  else if (t>22)
  {
  digitalWrite(8, HIGH);
  digitalWrite(7, LOW);
  digitalWrite(9, LOW);
  }
  else if (t>=35)
  {
  digitalWrite(9, HIGH);
  digitalWrite(7, LOW);
  digitalWrite(8, LOW);
  } 
  
}
